# Fritzing sketch Bluetooth_RC_Car (saved by Fritzing 0.9.3b)
breadboards: 1

parts:
  Part1 = Arduino Nano (Rev3.0)
  Part2 = Bluetooth HC-05 Macho
  R1 = Resistor [tolerance=±5% resistance=1k package=THT]
  R2 = Resistor [tolerance=±5% resistance=2k package=THT]
  S1 = H-Bridge with L298N
  M1 = DC Motor
  VCC2 = Battery block 9V
  J1 = Basic Servo
  SCW05B-1 = SCW05B-05

nets:
  GND: Part1.GND, Part2.GND, R2.Pin_0, S1.GND, VCC2.-, SCW05B-1.Vin_-
  N1: Part1.D2, Part2.TXD
  N2: Part1.D3, R1.Pin_1
  N3: Part1.D7, J1.pulse
  N4: Part1.D11/MOSI, S1.IN1
  N5: Part1.D12/MISO, S1.IN2
  VIN: Part1.VIN, Part2.VCC, S1.5V
  N6: Part2.RXD, R1.Pin_0, R2.Pin_1
  N7: S1.12V, VCC2.+, SCW05B-1.Vin_+
  N8: S1.ENA, S1.ENA-5V
  N9: S1.M1-01, M1.pin_2
  N10: S1.M1-02, M1.pin_1
  GND_2: J1.gnd, SCW05B-1.GND
  N11: J1.vcc, SCW05B-1.Vout_+

custom parts:
  H-Bridge with L298N: h-bridge
